// Logisim project CSO LAB2.circ as structural Verilog: 6 circuits, main circuit main
module main (
  input  in_1,
  input  in_2,
  input  in_3,
  input  in_4,
  input  in_5,
  input  in_6,
  input  in_7,
  input  in_8,
  input  in_9,
  output out_10,
  output out_11,
  output out_12,
  output out_13,
  output out_14
);

  wire full_adder_1_c_2, full_adder_2_c_2, full_adder_3_c_2;

  FULL_ADDER full_adder_1 (.C(in_1), .A(in_2), .B(in_3), .S(out_10), .C_2(full_adder_1_c_2));
  FULL_ADDER full_adder_2 (.C(in_4), .A(in_5), .B(full_adder_1_c_2), .S(out_11), .C_2(full_adder_2_c_2));
  FULL_ADDER full_adder_3 (.C(in_6), .A(in_7), .B(full_adder_2_c_2), .S(out_12), .C_2(full_adder_3_c_2));
  FULL_ADDER full_adder_4 (.C(in_8), .A(in_9), .B(full_adder_3_c_2), .S(out_13), .C_2(out_14));
endmodule

module HALF_ADDER (
  input  A,
  input  B,
  output S,
  output C
);

  wire nand_1_out, nand_2_out, nand_3_out;

  nand nand_1 (nand_1_out, A, B);
  nand nand_2 (nand_2_out, A, nand_1_out);
  nand nand_3 (nand_3_out, nand_1_out, B);
  nand nand_4 (S, nand_2_out, nand_3_out);
  nand nand_5 (C, nand_1_out, nand_1_out);
endmodule

module FULL_ADDER (
  input  C,
  input  A,
  input  B,
  output S,
  output C_2
);

  wire nand_1_out, nand_2_out, nand_3_out, nand_4_out, nand_5_out, nand_6_out, nand_7_out, nand_8_out,
       nand_10_out, nand_11_out, nand_12_out;

  nand nand_1 (nand_1_out, A, B);
  nand nand_2 (nand_2_out, A, nand_1_out);
  nand nand_3 (nand_3_out, nand_1_out, B);
  nand nand_4 (nand_4_out, nand_2_out, nand_3_out);
  nand nand_5 (nand_5_out, nand_1_out, nand_1_out);
  nand nand_6 (nand_6_out, C, nand_4_out);
  nand nand_7 (nand_7_out, C, nand_6_out);
  nand nand_8 (nand_8_out, nand_6_out, nand_4_out);
  nand nand_9 (S, nand_7_out, nand_8_out);
  nand nand_10 (nand_10_out, nand_6_out, nand_6_out);
  nand nand_11 (nand_11_out, nand_10_out, nand_10_out);
  nand nand_12 (nand_12_out, nand_5_out, nand_5_out);
  nand nand_13 (C_2, nand_11_out, nand_12_out);
endmodule

module _4_bit_adder (
  input  in_1,
  input  in_2,
  input  in_3,
  input  in_4,
  input  in_5,
  input  in_6,
  input  in_7,
  input  in_8,
  input  in_9,
  output out_10,
  output out_11,
  output out_12,
  output out_13,
  output out_14
);

  wire full_adder_1_c_2, full_adder_2_c_2, full_adder_3_c_2;

  FULL_ADDER full_adder_1 (.C(in_1), .A(in_2), .B(in_3), .S(out_10), .C_2(full_adder_1_c_2));
  FULL_ADDER full_adder_2 (.C(in_4), .A(in_5), .B(full_adder_1_c_2), .S(out_11), .C_2(full_adder_2_c_2));
  FULL_ADDER full_adder_3 (.C(in_6), .A(in_7), .B(full_adder_2_c_2), .S(out_12), .C_2(full_adder_3_c_2));
  FULL_ADDER full_adder_4 (.C(in_8), .A(in_9), .B(full_adder_3_c_2), .S(out_13), .C_2(out_14));
endmodule

module _4_BIT_SUBTRACTOR (
  input  in_1,
  input  in_2,
  input  in_3,
  input  in_4,
  input  in_5,
  input  in_6,
  input  in_7,
  input  in_8,
  input  in_9,
  output out_10,
  output out_11,
  output out_12,
  output out_13,
  output out_14
);

  wire full_adder_1_c_2, full_adder_2_c_2, full_adder_3_c_2, not_1_out, not_2_out, not_3_out, not_4_out;

  not not_1 (not_1_out, in_2);
  not not_2 (not_2_out, in_5);
  not not_3 (not_3_out, in_7);
  not not_4 (not_4_out, in_9);
  FULL_ADDER full_adder_1 (.C(in_1), .A(not_1_out), .B(in_3), .S(out_10), .C_2(full_adder_1_c_2));
  FULL_ADDER full_adder_2 (.C(in_4), .A(not_2_out), .B(full_adder_1_c_2), .S(out_11), .C_2(full_adder_2_c_2));
  FULL_ADDER full_adder_3 (.C(in_6), .A(not_3_out), .B(full_adder_2_c_2), .S(out_12), .C_2(full_adder_3_c_2));
  FULL_ADDER full_adder_4 (.C(in_8), .A(not_4_out), .B(full_adder_3_c_2), .S(out_13), .C_2(out_14));
endmodule

module _4_BIT_ADDER_SUBTRACTOR (
  input  in_1,
  input  in_2,
  input  in_3,
  input  in_4,
  input  in_5,
  input  in_6,
  input  in_7,
  input  in_8,
  input  in_9,
  output out_10,
  output out_11,
  output out_12,
  output out_13,
  output out_14
);

  wire full_adder_1_c_2, full_adder_2_c_2, full_adder_3_c_2, undriven, xor_1_out, xor_2_out, xor_3_out,
       xor_4_out;

  xor xor_1 (xor_1_out, in_3, undriven);
  xor xor_2 (xor_2_out, in_5, undriven);
  xor xor_3 (xor_3_out, in_7, undriven);
  xor xor_4 (xor_4_out, in_9, undriven);
  FULL_ADDER full_adder_1 (.C(in_2), .A(xor_1_out), .B(undriven), .S(out_10), .C_2(full_adder_1_c_2));
  FULL_ADDER full_adder_2 (.C(in_4), .A(xor_2_out), .B(full_adder_1_c_2), .S(out_11), .C_2(full_adder_2_c_2));
  FULL_ADDER full_adder_3 (.C(in_6), .A(xor_3_out), .B(full_adder_2_c_2), .S(out_12), .C_2(full_adder_3_c_2));
  FULL_ADDER full_adder_4 (.C(in_8), .A(xor_4_out), .B(full_adder_3_c_2), .S(out_13), .C_2(out_14));
endmodule
