// Logisim project CSO LAB4.circ as structural Verilog
module main (
  input  in_1,
  input  in_2,
  input  in_3,
  input  in_4,
  input  in_5,
  input  in_6,
  input  in_7,
  input  in_8,
  input  in_9,
  output out_10,
  output out_11,
  output out_12,
  output out_13,
  output out_14
);

  wire full_adder_1_c_2, full_adder_2_c_2, full_adder_3_c_2;

  FULL_ADDER full_adder_1 (.C(in_1), .A(in_2), .B(in_3), .S(out_10), .C_2(full_adder_1_c_2));
  FULL_ADDER full_adder_2 (.C(in_4), .A(in_5), .B(full_adder_1_c_2), .S(out_11), .C_2(full_adder_2_c_2));
  FULL_ADDER full_adder_3 (.C(in_6), .A(in_7), .B(full_adder_2_c_2), .S(out_12), .C_2(full_adder_3_c_2));
  FULL_ADDER full_adder_4 (.C(in_8), .A(in_9), .B(full_adder_3_c_2), .S(out_13), .C_2(out_14));
endmodule

module HALF_ADDER (
  input  A,
  input  B,
  output S,
  output C
);

  wire nand_1_out, nand_2_out, nand_3_out;

  nand nand_1 (nand_1_out, A, B);
  nand nand_2 (nand_2_out, A, nand_1_out);
  nand nand_3 (nand_3_out, nand_1_out, B);
  nand nand_4 (S, nand_2_out, nand_3_out);
  nand nand_5 (C, nand_1_out, nand_1_out);
endmodule

module FULL_ADDER (
  input  C,
  input  A,
  input  B,
  output S,
  output C_2
);

  wire nand_1_out, nand_2_out, nand_3_out, nand_4_out, nand_5_out, nand_6_out, nand_7_out, nand_8_out,
       nand_10_out, nand_11_out, nand_12_out;

  nand nand_1 (nand_1_out, A, B);
  nand nand_2 (nand_2_out, A, nand_1_out);
  nand nand_3 (nand_3_out, nand_1_out, B);
  nand nand_4 (nand_4_out, nand_2_out, nand_3_out);
  nand nand_5 (nand_5_out, nand_1_out, nand_1_out);
  nand nand_6 (nand_6_out, C, nand_4_out);
  nand nand_7 (nand_7_out, C, nand_6_out);
  nand nand_8 (nand_8_out, nand_6_out, nand_4_out);
  nand nand_9 (S, nand_7_out, nand_8_out);
  nand nand_10 (nand_10_out, nand_6_out, nand_6_out);
  nand nand_11 (nand_11_out, nand_10_out, nand_10_out);
  nand nand_12 (nand_12_out, nand_5_out, nand_5_out);
  nand nand_13 (C_2, nand_11_out, nand_12_out);
endmodule

module _4_BIT_ADDER (
  input  A0,
  input  B0,
  input  in_3,
  input  A1,
  input  B1,
  input  A2,
  input  B2,
  input  A3,
  input  B3,
  output S0,
  output S1,
  output S2,
  output S3,
  output C
);

  wire full_adder_1_c_2, full_adder_2_c_2, full_adder_3_c_2;

  FULL_ADDER full_adder_1 (.C(A0), .A(B0), .B(in_3), .S(S0), .C_2(full_adder_1_c_2));
  FULL_ADDER full_adder_2 (.C(A1), .A(B1), .B(full_adder_1_c_2), .S(S1), .C_2(full_adder_2_c_2));
  FULL_ADDER full_adder_3 (.C(A2), .A(B2), .B(full_adder_2_c_2), .S(S2), .C_2(full_adder_3_c_2));
  FULL_ADDER full_adder_4 (.C(A3), .A(B3), .B(full_adder_3_c_2), .S(S3), .C_2(C));
endmodule

module _4_BIT_SUBTRACTOR (
  input  A0,
  input  BO,
  input  in_3,
  input  A1,
  input  B1,
  input  A2,
  input  B2,
  input  A3,
  input  B3,
  output D0,
  output D1,
  output D2,
  output D3,
  output C
);

  wire full_adder_1_c_2, full_adder_2_c_2, full_adder_3_c_2, not_1_out, not_2_out, not_3_out, not_4_out;

  not not_1 (not_1_out, BO);
  not not_2 (not_2_out, B1);
  not not_3 (not_3_out, B2);
  not not_4 (not_4_out, B3);
  FULL_ADDER full_adder_1 (.C(A0), .A(not_1_out), .B(in_3), .S(D0), .C_2(full_adder_1_c_2));
  FULL_ADDER full_adder_2 (.C(A1), .A(not_2_out), .B(full_adder_1_c_2), .S(D1), .C_2(full_adder_2_c_2));
  FULL_ADDER full_adder_3 (.C(A2), .A(not_3_out), .B(full_adder_2_c_2), .S(D2), .C_2(full_adder_3_c_2));
  FULL_ADDER full_adder_4 (.C(A3), .A(not_4_out), .B(full_adder_3_c_2), .S(D3), .C_2(C));
endmodule

module _4_BIT_ADDER_SUBTRACTOR (
  input  A0,
  input  B0,
  input  M,
  input  A1,
  input  B1,
  input  A2,
  input  B2,
  input  A3,
  input  B3,
  output R0,
  output R1,
  output R2,
  output R3,
  output C
);

  wire full_adder_1_c_2, full_adder_2_c_2, full_adder_3_c_2, xor_1_out, xor_2_out, xor_3_out, xor_4_out;

  xor xor_1 (xor_1_out, B0, M);
  xor xor_2 (xor_2_out, B1, M);
  xor xor_3 (xor_3_out, B2, M);
  xor xor_4 (xor_4_out, B3, M);
  FULL_ADDER full_adder_1 (.C(A0), .A(xor_1_out), .B(M), .S(R0), .C_2(full_adder_1_c_2));
  FULL_ADDER full_adder_2 (.C(A1), .A(xor_2_out), .B(full_adder_1_c_2), .S(R1), .C_2(full_adder_2_c_2));
  FULL_ADDER full_adder_3 (.C(A2), .A(xor_3_out), .B(full_adder_2_c_2), .S(R2), .C_2(full_adder_3_c_2));
  FULL_ADDER full_adder_4 (.C(A3), .A(xor_4_out), .B(full_adder_3_c_2), .S(R3), .C_2(C));
endmodule

module _4_BIT_AS (
  input  in_1,
  input  in_2,
  input  in_3,
  input  in_4,
  input  in_5,
  input  in_6,
  input  in_7,
  input  in_8,
  input  in_9,
  input  in_10,
  output out_11,
  output out_12,
  output out_13,
  output out_14,
  output out_15
);

  wire full_adder_1_c_2, full_adder_2_c_2, full_adder_3_c_2, not_1_out, not_2_out, not_3_out, undriven,
       xor_1_out;

  xor xor_1 (xor_1_out, in_3, undriven);
  not not_1 (not_1_out, in_6);
  not not_2 (not_2_out, in_8);
  not not_3 (not_3_out, in_10);
  FULL_ADDER full_adder_1 (.C(in_2), .A(xor_1_out), .B(in_4), .S(out_11), .C_2(full_adder_1_c_2));
  FULL_ADDER full_adder_2 (.C(in_5), .A(not_1_out), .B(full_adder_1_c_2), .S(out_12), .C_2(full_adder_2_c_2));
  FULL_ADDER full_adder_3 (.C(in_7), .A(not_2_out), .B(full_adder_2_c_2), .S(out_13), .C_2(full_adder_3_c_2));
  FULL_ADDER full_adder_4 (.C(in_9), .A(not_3_out), .B(full_adder_3_c_2), .S(out_14), .C_2(out_15));
endmodule

module D_Flip_Flop (
  input  in_1,
  input  in_2,
  output out_3,
  output out_4
);

  D_Flip_Flop_part d_ff_1 (.clk(in_1), .D(in_2), .Q(out_3), .Qn(out_4));  // open: preset, en, reset
endmodule

module Mod_8_counter (
  input  INPUT,
  output C2,
  output C1,
  output C0
);

  wire and_1_out, and_2_out, and_3_out, and_4_out, and_5_out, and_6_out, clock_1_out, not_1_out, not_2_out,
       not_3_out, not_4_out, not_5_out, not_6_out, or_1_out, or_2_out;

  Clock clock_1 (.out(clock_1_out));
  not not_1 (not_1_out, C2);
  and and_1 (and_1_out, not_1_out, C1, C0);
  and and_2 (and_2_out, C2, not_2_out);
  not not_2 (not_2_out, C1);
  and and_3 (and_3_out, C2, not_3_out);
  not not_3 (not_3_out, C0);
  not not_4 (not_4_out, C1);
  and and_4 (and_4_out, not_4_out, C0);
  and and_5 (and_5_out, C1, not_5_out);
  not not_5 (not_5_out, C0);
  and and_6 (and_6_out, clock_1_out, INPUT);
  or or_1 (or_1_out, and_1_out, and_2_out, and_3_out);
  or or_2 (or_2_out, and_4_out, and_5_out);
  not not_6 (not_6_out, C0);
  D_Flip_Flop d_flip_flop_1 (.in_1(and_6_out), .in_2(or_1_out), .out_3(C2));  // open: out_4
  D_Flip_Flop d_flip_flop_2 (.in_1(and_6_out), .in_2(or_2_out), .out_3(C1));  // open: out_4
  D_Flip_Flop d_flip_flop_3 (.in_1(and_6_out), .in_2(not_6_out), .out_3(C0));  // open: out_4

  // Notes on the sheet:
  //   CLK
  //   C2
  //   C1
  //   C0
endmodule

module T_flip_flop (
  input  in_1,
  input  in_2,
  output out_3,
  output out_4
);

  T_Flip_Flop t_ff_1 (.clk(in_1), .T(in_2), .Q(out_3), .Qn(out_4));  // open: preset, reset, en
endmodule

module RIPPLE_COUNTER (
  input  in_1,
  output Q2,
  output Q1,
  output Q0
);

  wire clock_1_out, t_flip_flop_1_out_4, t_flip_flop_2_out_4;

  Clock clock_1 (.out(clock_1_out));
  T_flip_flop t_flip_flop_1 (.out_3(Q0), .in_1(clock_1_out), .in_2(in_1), .out_4(t_flip_flop_1_out_4));
  T_flip_flop t_flip_flop_2 (.out_3(Q1), .in_1(t_flip_flop_1_out_4), .in_2(in_1), .out_4(t_flip_flop_2_out_4));
  T_flip_flop t_flip_flop_3 (.out_3(Q2), .in_1(t_flip_flop_2_out_4), .in_2(in_1));  // open: out_4
endmodule

module _7_segment_display (
  input  A,
  input  B,
  input  C,
  input  D,
  output a_2,
  output b_2,
  output c_2,
  output d_2,
  output e,
  output f,
  output g
);

  wire and_1_out, and_2_out, and_3_out, and_4_out, and_5_out, and_6_out, and_7_out, and_8_out, and_9_out,
       and_10_out, not_1_out, not_2_out, not_3_out, not_4_out;

  not not_1 (not_1_out, A);
  not not_2 (not_2_out, B);
  not not_3 (not_3_out, C);
  not not_4 (not_4_out, D);
  and and_1 (and_1_out, B, D);
  and and_2 (and_2_out, not_2_out, not_4_out);
  and and_3 (and_3_out, D, C);
  and and_4 (and_4_out, not_4_out, not_3_out);
  and and_5 (and_5_out, not_4_out, not_2_out);
  and and_6 (and_6_out, not_2_out, C);
  and and_7 (and_7_out, C, not_4_out);
  and and_8 (and_8_out, B, not_3_out, D);
  and and_9 (and_9_out, B, not_3_out);
  and and_10 (and_10_out, B, not_4_out);
  or or_1 (a_2, and_1_out, and_2_out, C, A);
  or or_2 (b_2, and_3_out, and_4_out, not_2_out);
  or or_3 (c_2, D, not_3_out, B);
  or or_4 (d_2, and_5_out, and_6_out, and_7_out, and_8_out, A);
  or or_5 (e, and_7_out, and_5_out);
  or or_6 (f, and_4_out, and_9_out, and_10_out, A);
  or or_7 (g, and_9_out, and_7_out, and_6_out, A);
  _7_Segment_Display u_7_segment_display_1 (.g(g), .f(f), .a(a_2), .b(b_2), .e(e), .d(d_2), .c(c_2));  // open: dp
endmodule

module _16x1_MUX_USING_2X1_MUX (
  input  in_1,
  input  in_2,
  input  in_3,
  output out_4
);

  Multiplexer #(.enable("false")) multiplexer_1 (.in0(in_1), .in1(in_2), .out(out_4), .sel(in_3));
endmodule

module _2X1_MUX (
  input  in_1,
  input  in_2,
  input  in_3,
  output out_4
);

  Multiplexer #(.enable("false")) multiplexer_1 (.in0(in_1), .in1(in_2), .out(out_4), .sel(in_3));
endmodule

module _16X1_MUX (
  input  I0,
  input  S3,
  input  S2,
  input  S1,
  input  S0,
  input  I1,
  input  I2,
  input  I3,
  input  I4,
  input  I5,
  input  I6,
  input  I7,
  input  I8,
  input  I9,
  input  I10,
  input  I11,
  input  I12,
  input  I13,
  input  I14,
  input  I15,
  output Y
);

  wire n2x1_mux_1_out_4, n2x1_mux_2_out_4, n2x1_mux_3_out_4, n2x1_mux_4_out_4, n2x1_mux_5_out_4,
       n2x1_mux_6_out_4, n2x1_mux_7_out_4, n2x1_mux_8_out_4, n2x1_mux_9_out_4, n2x1_mux_10_out_4,
       n2x1_mux_11_out_4, n2x1_mux_12_out_4, n2x1_mux_13_out_4, n2x1_mux_14_out_4;

  _2X1_MUX u_2x1_mux_1 (.in_1(I0), .in_2(I1), .out_4(n2x1_mux_1_out_4), .in_3(S0));
  _2X1_MUX u_2x1_mux_2 (.in_1(I2), .in_2(I3), .out_4(n2x1_mux_2_out_4), .in_3(S0));
  _2X1_MUX u_2x1_mux_3 (.in_1(I4), .in_2(I5), .out_4(n2x1_mux_3_out_4), .in_3(S0));
  _2X1_MUX u_2x1_mux_4 (.in_1(I6), .in_2(I7), .out_4(n2x1_mux_4_out_4), .in_3(S0));
  _2X1_MUX u_2x1_mux_5 (.in_1(I8), .in_2(I9), .out_4(n2x1_mux_5_out_4), .in_3(S0));
  _2X1_MUX u_2x1_mux_6 (.in_1(I10), .in_2(I11), .out_4(n2x1_mux_6_out_4), .in_3(S0));
  _2X1_MUX u_2x1_mux_7 (.in_1(I12), .in_2(I13), .out_4(n2x1_mux_7_out_4), .in_3(S0));
  _2X1_MUX u_2x1_mux_8 (.in_1(I14), .in_2(I15), .out_4(n2x1_mux_8_out_4), .in_3(S0));
  _2X1_MUX u_2x1_mux_9 (.in_1(n2x1_mux_1_out_4), .in_2(n2x1_mux_2_out_4), .out_4(n2x1_mux_9_out_4), .in_3(S1));
  _2X1_MUX u_2x1_mux_10 (.in_1(n2x1_mux_3_out_4), .in_2(n2x1_mux_4_out_4), .out_4(n2x1_mux_10_out_4), .in_3(S1));
  _2X1_MUX u_2x1_mux_11 (.in_1(n2x1_mux_5_out_4), .in_2(n2x1_mux_6_out_4), .out_4(n2x1_mux_11_out_4), .in_3(S1));
  _2X1_MUX u_2x1_mux_12 (.in_1(n2x1_mux_7_out_4), .in_2(n2x1_mux_8_out_4), .out_4(n2x1_mux_12_out_4), .in_3(S1));
  _2X1_MUX u_2x1_mux_13 (.in_1(n2x1_mux_9_out_4), .in_2(n2x1_mux_10_out_4), .out_4(n2x1_mux_13_out_4), .in_3(S2));
  _2X1_MUX u_2x1_mux_14 (.in_1(n2x1_mux_11_out_4), .in_2(n2x1_mux_12_out_4), .out_4(n2x1_mux_14_out_4), .in_3(S2));
  _2X1_MUX u_2x1_mux_15 (.in_1(n2x1_mux_13_out_4), .in_2(n2x1_mux_14_out_4), .out_4(Y), .in_3(S3));
endmodule

module ARITHMETIC_SHIFT_REGISTER (
  input  Input,
  input  Input_2,
  output Q3,
  output Q2,
  output Q1,
  output Q0,
  output Q3_2,
  output Q2_2,
  output Q1_2,
  output Q0_2
);

  wire clock_1_out, clock_2_out;

  Clock clock_1 (.out(clock_1_out));
  Clock clock_2 (.out(clock_2_out));
  D_Flip_Flop d_flip_flop_1 (.in_1(clock_1_out), .in_2(Input), .out_3(Q3));  // open: out_4
  D_Flip_Flop d_flip_flop_2 (.in_1(clock_2_out), .in_2(Q2_2), .out_3(Q3_2));  // open: out_4
  D_Flip_Flop d_flip_flop_3 (.in_1(clock_1_out), .in_2(Q3), .out_3(Q2));  // open: out_4
  D_Flip_Flop d_flip_flop_4 (.in_1(clock_2_out), .in_2(Q1_2), .out_3(Q2_2));  // open: out_4
  D_Flip_Flop d_flip_flop_5 (.in_1(clock_1_out), .in_2(Q2), .out_3(Q1));  // open: out_4
  D_Flip_Flop d_flip_flop_6 (.in_1(clock_2_out), .in_2(Q0_2), .out_3(Q1_2));  // open: out_4
  D_Flip_Flop d_flip_flop_7 (.in_1(clock_1_out), .in_2(Q1), .out_3(Q0));  // open: out_4
  D_Flip_Flop d_flip_flop_8 (.in_1(clock_2_out), .in_2(Input_2), .out_3(Q0_2));  // open: out_4

  // Notes on the sheet:
  //   Clock
  //   Clock
  //   MSB
  //   MSB
  //   RIGHT SHIFT REGISTER
  //   LEFT SHIFT REGISTER
  //   LSB
  //   LSB
endmodule

module ARITHMETIC_SHIFT (
  input  in_1,
  input  S,
  input  in_3,
  input  in_4,
  input  in_5,
  input  in_6,
  input  in_7,
  input  S_2,
  input  in_9,
  input  in_10,
  input  in_11,
  input  in_12,
  output Q3,
  output Q2,
  output Q1,
  output Q0,
  output Q3_2,
  output Q2_2,
  output Q1_2,
  output Q0_2
);

  wire clock_1_out, clock_2_out, multiplexer_1_out, multiplexer_2_out, multiplexer_3_out, multiplexer_4_out,
       multiplexer_5_out, multiplexer_6_out, multiplexer_7_out, multiplexer_8_out;

  Clock clock_1 (.out(clock_1_out));
  D_Flip_Flop d_flip_flop_1 (.in_1(clock_1_out), .in_2(multiplexer_1_out), .out_3(Q3));  // open: out_4
  Multiplexer #(.enable("false")) multiplexer_1 (.in0(in_1), .in1(in_3), .out(multiplexer_1_out), .sel(S));
  Clock clock_2 (.out(clock_2_out));
  D_Flip_Flop d_flip_flop_2 (.in_1(clock_2_out), .in_2(multiplexer_2_out), .out_3(Q3_2));  // open: out_4
  Multiplexer #(.enable("false")) multiplexer_2 (.in0(Q2_2), .in1(in_9), .out(multiplexer_2_out), .sel(S_2));
  D_Flip_Flop d_flip_flop_3 (.in_1(clock_1_out), .in_2(multiplexer_3_out), .out_3(Q2));  // open: out_4
  Multiplexer #(.enable("false")) multiplexer_3 (.in0(Q3), .in1(in_4), .out(multiplexer_3_out), .sel(S));
  D_Flip_Flop d_flip_flop_4 (.in_1(clock_2_out), .in_2(multiplexer_4_out), .out_3(Q2_2));  // open: out_4
  Multiplexer #(.enable("false")) multiplexer_4 (.in0(Q1_2), .in1(in_10), .out(multiplexer_4_out), .sel(S_2));
  D_Flip_Flop d_flip_flop_5 (.in_1(clock_1_out), .in_2(multiplexer_5_out), .out_3(Q1));  // open: out_4
  Multiplexer #(.enable("false")) multiplexer_5 (.in0(Q2), .in1(in_5), .out(multiplexer_5_out), .sel(S));
  D_Flip_Flop d_flip_flop_6 (.in_1(clock_2_out), .in_2(multiplexer_6_out), .out_3(Q1_2));  // open: out_4
  Multiplexer #(.enable("false")) multiplexer_6 (.in0(Q0_2), .in1(in_11), .out(multiplexer_6_out), .sel(S_2));
  D_Flip_Flop d_flip_flop_7 (.in_1(clock_1_out), .in_2(multiplexer_7_out), .out_3(Q0));  // open: out_4
  Multiplexer #(.enable("false")) multiplexer_7 (.in0(Q1), .in1(in_6), .out(multiplexer_7_out), .sel(S));
  Multiplexer #(.enable("false")) multiplexer_8 (.in0(in_7), .in1(in_12), .out(multiplexer_8_out), .sel(S_2));
  D_Flip_Flop d_flip_flop_8 (.in_1(clock_2_out), .in_2(multiplexer_8_out), .out_3(Q0_2));  // open: out_4

  // Notes on the sheet:
  //   Clock
  //   Clock
  //   I0
  //   I0
  //   MSB
  //   I1
  //   MSB
  //   I1
  //   I2
  //   LOGICAL RIGHT SHIFT REGISTER
  //   LOGICAL/ ARITHMETIC LEFT SHIFT REGISTER
  //   I2
  //   I3
  //   I3
  //   LSB
  //   LSB
endmodule

module ARITH_RIGHT (
  input  in_1,
  input  S,
  input  in_3,
  input  in_4,
  input  in_5,
  input  in_6,
  output Q3,
  output Q2,
  output Q1,
  output Q0
);

  wire clock_1_out, multiplexer_1_out, multiplexer_2_out, multiplexer_3_out, multiplexer_4_out;

  Clock clock_1 (.out(clock_1_out));
  D_Flip_Flop d_flip_flop_1 (.in_1(clock_1_out), .in_2(multiplexer_1_out), .out_3(Q3));  // open: out_4
  Multiplexer #(.enable("false")) multiplexer_1 (.in0(in_1), .in1(in_3), .out(multiplexer_1_out), .sel(S));
  D_Flip_Flop d_flip_flop_2 (.in_1(clock_1_out), .in_2(multiplexer_2_out), .out_3(Q2));  // open: out_4
  Multiplexer #(.enable("false")) multiplexer_2 (.in0(Q3), .in1(in_3), .out(multiplexer_2_out), .sel(S));
  D_Flip_Flop d_flip_flop_3 (.in_1(clock_1_out), .in_2(multiplexer_3_out), .out_3(Q1));  // open: out_4
  Multiplexer #(.enable("false")) multiplexer_3 (.in0(Q2), .in1(in_4), .out(multiplexer_3_out), .sel(S));
  D_Flip_Flop d_flip_flop_4 (.in_1(clock_1_out), .in_2(multiplexer_4_out), .out_3(Q0));  // open: out_4
  Multiplexer #(.enable("false")) multiplexer_4 (.in0(Q1), .in1(in_5), .out(multiplexer_4_out), .sel(S));

  // Notes on the sheet:
  //   Clock
  //   MSB
  //   I0
  //   I1
  //   ARITHMETIC RIGHT SHIFT REGISTER
  //   I2
  //   I3
  //   LSB
endmodule

module NEW_ARITH (
  input  in_1,
  input  S,
  input  in_3,
  input  in_4,
  input  in_5,
  input  in_6,
  output Q3,
  output Q2,
  output Q1,
  output Q0
);

  wire clock_1_out, d_flip_flop_1_out_3, multiplexer_1_out, multiplexer_2_out, multiplexer_3_out,
       multiplexer_4_out;

  Clock clock_1 (.out(clock_1_out));
  D_Flip_Flop d_flip_flop_1 (.in_1(clock_1_out), .in_2(multiplexer_1_out), .out_3(d_flip_flop_1_out_3));  // open: out_4
  Multiplexer #(.enable("false")) multiplexer_1 (.in0(in_1), .in1(in_3), .out(multiplexer_1_out), .sel(S));
  D_Flip_Flop d_flip_flop_2 (.in_1(clock_1_out), .in_2(multiplexer_2_out), .out_3(Q2));  // open: out_4
  Multiplexer #(.enable("false")) multiplexer_2 (
    .in0(d_flip_flop_1_out_3), .in1(in_4), .out(multiplexer_2_out), .sel(S));
  D_Flip_Flop d_flip_flop_3 (.in_1(clock_1_out), .in_2(multiplexer_3_out), .out_3(Q1));  // open: out_4
  Multiplexer #(.enable("false")) multiplexer_3 (.in0(Q2), .in1(in_5), .out(multiplexer_3_out), .sel(S));
  D_Flip_Flop d_flip_flop_4 (.in_1(clock_1_out), .in_2(multiplexer_4_out), .out_3(Q0));  // open: out_4
  Multiplexer #(.enable("false")) multiplexer_4 (.in0(Q1), .in1(in_6), .out(multiplexer_4_out), .sel(S));

  assign Q3 = in_3;

  // Notes on the sheet:
  //   Clock
  //   MSB
  //   I2
  //   ARITHMETIC RIGHT SHIFT REGISTER
  //   I3
  //   LSB
endmodule
