// Logisim project FULL ADDER USING HALF ADDER OPTIMISED.circ as structural Verilog: 1 circuit, main circuit main
module main (
  input  C,
  input  A,
  input  B,
  output S,
  output S0,
  output C1,
  output C_2,
  output C0
);

  wire nand_1_out, nand_2_out, nand_3_out, nand_6_out, nand_7_out, nand_8_out, nand_11_out, nand_12_out;

  nand nand_1 (nand_1_out, A, B);
  nand nand_2 (nand_2_out, A, nand_1_out);
  nand nand_3 (nand_3_out, nand_1_out, B);
  nand nand_4 (S0, nand_2_out, nand_3_out);
  nand nand_5 (C0, nand_1_out, nand_1_out);
  nand nand_6 (nand_6_out, C, S0);
  nand nand_7 (nand_7_out, C, nand_6_out);
  nand nand_8 (nand_8_out, nand_6_out, S0);
  nand nand_9 (S, nand_7_out, nand_8_out);
  nand nand_10 (C1, nand_6_out, nand_6_out);
  nand nand_11 (nand_11_out, C1, C1);
  nand nand_12 (nand_12_out, C0, C0);
  nand nand_13 (C_2, nand_11_out, nand_12_out);
endmodule
