// Logisim project FULL ADDER USING HALF ADDER.circ as structural Verilog: 1 circuit, main circuit main
module main (
  input  C,
  input  A,
  input  B,
  output S,
  output S0,
  output C1,
  output C_2,
  output C0
);

  wire nand_1_out, nand_2_out, nand_3_out, nand_4_out, nand_5_out, nand_8_out, nand_9_out, nand_10_out,
       nand_11_out, nand_12_out, nand_15_out, nand_16_out;

  nand nand_1 (nand_1_out, B, B);
  nand nand_2 (nand_2_out, A, A);
  nand nand_3 (nand_3_out, nand_1_out, A);
  nand nand_4 (nand_4_out, B, nand_2_out);
  nand nand_5 (nand_5_out, A, B);
  nand nand_6 (S0, nand_3_out, nand_4_out);
  nand nand_7 (C0, nand_5_out, nand_5_out);
  nand nand_8 (nand_8_out, S0, S0);
  nand nand_9 (nand_9_out, C, C);
  nand nand_10 (nand_10_out, nand_8_out, C);
  nand nand_11 (nand_11_out, S0, nand_9_out);
  nand nand_12 (nand_12_out, C, S0);
  nand nand_13 (S, nand_10_out, nand_11_out);
  nand nand_14 (C1, nand_12_out, nand_12_out);
  nand nand_15 (nand_15_out, C1, C1);
  nand nand_16 (nand_16_out, C0, C0);
  nand nand_17 (C_2, nand_15_out, nand_16_out);

  // Notes on the sheet:
  //   C1
endmodule
