// Logisim project Logical and arithmetic shift.circ as structural Verilog: 1 circuit, main circuit main
module main (
  input  in_1,
  input  in_2,
  input  I2,
  input  I1,
  input  I3,
  input  in_6,
  input  I3_2,
  input  in_8,
  input  in_9,
  output out_10,
  output Q2,
  output out_12,
  output out_13
);

  wire clock_1_out, multiplexer_1_out, multiplexer_2_out, multiplexer_3_out, multiplexer_4_out;

  Clock clock_1 (.out(clock_1_out));
  Multiplexer #(.enable("false")) multiplexer_1 (.in0(in_1), .in1(I3), .out(multiplexer_1_out), .sel(in_6));
  D_Flip_Flop #(.trigger("falling")) d_ff_1 (
    .clk(clock_1_out), .D(multiplexer_1_out), .Q(out_10));  // open: Qn, preset, en, reset
  Multiplexer #(.enable("false")) multiplexer_2 (.in0(out_10), .in1(in_2), .out(multiplexer_2_out), .sel(I3_2));
  D_Flip_Flop #(.trigger("falling")) d_ff_2 (
    .clk(clock_1_out), .D(multiplexer_2_out), .Q(Q2));  // open: Qn, preset, en, reset
  Multiplexer #(.enable("false")) multiplexer_3 (.in0(Q2), .in1(I2), .out(multiplexer_3_out), .sel(in_8));
  D_Flip_Flop #(.trigger("falling")) d_ff_3 (
    .clk(clock_1_out), .D(multiplexer_3_out), .Q(out_12));  // open: Qn, preset, en, reset
  Multiplexer #(.enable("false")) multiplexer_4 (.in0(out_12), .in1(I1), .out(multiplexer_4_out), .sel(in_9));
  D_Flip_Flop #(.trigger("falling")) d_ff_4 (
    .clk(clock_1_out), .D(multiplexer_4_out), .Q(out_13));  // open: Qn, preset, en, reset

  // Notes on the sheet:
  //   I0
endmodule
