// Logisim project left_and_right_shift.circ as structural Verilog: 1 circuit, main circuit main
module main (
  input  MODE,
  input  DL,
  input  DR,
  output out_4,
  output out_5,
  output Q1,
  output out_7
);

  wire and_1_out, and_2_out, and_3_out, and_4_out, and_5_out, and_6_out, and_7_out, and_8_out, clock_1_out,
       not_1_out, or_1_out, or_2_out, or_3_out, or_4_out;

  not not_1 (not_1_out, MODE);
  and and_1 (and_1_out, DR, MODE);
  or or_1 (or_1_out, and_1_out, and_2_out);
  Clock clock_1 (.out(clock_1_out));
  and and_2 (and_2_out, not_1_out, out_5);
  and and_3 (and_3_out, not_1_out, Q1);
  and and_4 (and_4_out, out_4, MODE);
  or or_2 (or_2_out, and_4_out, and_3_out);
  D_Flip_Flop #(.trigger("falling")) d_ff_1 (
    .clk(clock_1_out), .D(or_1_out), .Q(out_4));  // open: Qn, preset, en, reset
  and and_5 (and_5_out, out_5, MODE);
  D_Flip_Flop #(.trigger("falling")) d_ff_2 (
    .clk(clock_1_out), .D(or_2_out), .Q(out_5));  // open: Qn, preset, en, reset
  and and_6 (and_6_out, not_1_out, out_7);
  or or_3 (or_3_out, and_5_out, and_6_out);
  and and_7 (and_7_out, Q1, MODE);
  D_Flip_Flop #(.trigger("falling")) d_ff_3 (.clk(clock_1_out), .D(or_3_out), .Q(Q1));  // open: Qn, preset, en, reset
  and and_8 (and_8_out, not_1_out, DL);
  or or_4 (or_4_out, and_7_out, and_8_out);
  D_Flip_Flop #(.trigger("falling")) d_ff_4 (
    .clk(clock_1_out), .D(or_4_out), .Q(out_7));  // open: Qn, preset, en, reset

  // Notes on the sheet:
  //   CLOCK
  //   Q3
  //   Q2
  //   Q0
endmodule
